# Fritzing sketch display_7s (saved by Fritzing 0.9.3b)
breadboards: 1

parts:
  U1 = NodeMCU v3.0
  R1 = Resistor [tolerance=±5% resistance=330 package=THT]
  7_Segment1 = 7 Segment Display
  R2 = Resistor [tolerance=±5% resistance=330 package=THT]
  R4 = Resistor [tolerance=±5% resistance=330 package=THT]
  R5 = Resistor [tolerance=±5% resistance=330 package=THT]
  R6 = Resistor [tolerance=±5% resistance=330 package=THT]
  R7 = Resistor [tolerance=±5% resistance=330 package=THT]
  R8 = Resistor [tolerance=±5% resistance=330 package=THT]

nets:
  N1: U1.D1, R4.Pin_1
  N2: U1.D2, R1.Pin_1
  N3: U1.D3, R2.Pin_1
  N4: U1.D4, R8.Pin_1
  N5: U1.GND, 7_Segment1.common_anode
  N6: U1.D5, R6.Pin_1
  N7: U1.D6, R7.Pin_1
  N8: U1.D7, R5.Pin_1
  N9: R1.Pin_0, 7_Segment1.Segment_B
  N10: 7_Segment1.Segment_G, R5.Pin_0
  N11: 7_Segment1.Segment_F, R7.Pin_0
  N12: 7_Segment1.Segment_E, R6.Pin_0
  N13: 7_Segment1.Segment_D, R8.Pin_0
  N14: 7_Segment1.Segment_C, R2.Pin_0
  N15: 7_Segment1.Segment_A, R4.Pin_0

custom parts:
  NodeMCU v3.0: NodeMCU v3 Lua WIFI Development Board
