# Fritzing sketch rgb_basic (saved by Fritzing 0.9.3b)
breadboards: 1

parts:
  LED1 = RGB LED (com. cathode, rgb) [package="5 mm [THT]"]
  U2 = NodeMCU v3.0
  R2 = Resistor [tolerance=±5% resistance=330 package=THT]
  R3 = Resistor [tolerance=±5% resistance=330 package=THT]
  R4 = Resistor [tolerance=±5% resistance=330 package=THT]

nets:
  N1: LED1.red_anode, R4.Pin_0
  N2: LED1.common_cathode, U2.GND
  N3: LED1.green_anode, R3.Pin_0
  N4: LED1.blue_anode, R2.Pin_0
  N5: U2.D1, R4.Pin_1
  N6: U2.D2, R3.Pin_1
  N7: U2.D3, R2.Pin_1

custom parts:
  NodeMCU v3.0: NodeMCU v3 Lua WIFI Development Board
