# Fritzing sketch servo_btn (saved by Fritzing 0.9.3b)
breadboards: 1

parts:
  J1 = Basic Servo
  U1 = NodeMCU v3.0
  R1 = Resistor [tolerance=±5% resistance=1k package=THT]
  S1 = Pushbutton [package="[THT]"]
  R2 = Resistor [tolerance=±5% resistance=1k package=THT]
  S2 = Pushbutton [package="[THT]"]

nets:
  GND: J1.gnd, U1.GND, R1.Pin_0, R2.Pin_0
  VCC: J1.vcc, U1.3V3, S1.Pin_1, S1.Pin_2, S2.Pin_1, S2.Pin_2
  N1: J1.pulse, U1.D1
  N2: U1.D2, R1.Pin_1, S1.Pin_3, S1.Pin_4
  N3: U1.D3, R2.Pin_1, S2.Pin_3, S2.Pin_4

custom parts:
  NodeMCU v3.0: NodeMCU v3 Lua WIFI Development Board
