# Fritzing sketch servo_pot (saved by Fritzing 0.9.3b)
breadboards: 1

parts:
  J1 = Basic Servo
  U1 = NodeMCU v3.0
  R1 = Rotary Potentiometer (Small) [maximum_resistance=100kΩ package=THT]
  PSU1 = Adjustable Breadboard Power Supply

nets:
  GND: J1.gnd, U1.GND, R1.leg1, PSU1.Vout-
  N1: J1.vcc, PSU1.Vout+
  N2: J1.pulse, U1.D1
  N3: U1.3V3, R1.leg2
  N4: U1.A0, R1.wiper

custom parts:
  NodeMCU v3.0: NodeMCU v3 Lua WIFI Development Board
