# Fritzing sketch ultrasonic_base (saved by Fritzing 0.9.3b)
breadboards: 1

parts:
  hc-sr1 = hc-sr04
  U1 = NodeMCU v3.0

nets:
  N1: hc-sr1.VCC, U1.VU
  N2: hc-sr1.Trig, U1.D0
  N3: hc-sr1.Echo, U1.D1
  GND: hc-sr1.GND, U1.GND

custom parts:
  NodeMCU v3.0: NodeMCU v3 Lua WIFI Development Board
