# Fritzing sketch led_pwm_bt (saved by Fritzing 0.9.3b)
breadboards: 1

parts:
  U1 = NodeMCU v3.0
  LED1 = LED - 5mm [color="Red (633nm)" package="5 mm [THT]"]
  R1 = Resistor [tolerance=±5% resistance=330 package=THT]
  S1 = Pushbutton [package="[THT]"]
  R2 = Resistor [tolerance=±5% resistance=1k package=THT]
  S2 = Pushbutton [package="[THT]"]
  R3 = Resistor [tolerance=±5% resistance=1k package=THT]

nets:
  N1: U1.D1, LED1.anode
  N2: U1.D2, S2.Pin_3, S2.Pin_4, R3.Pin_1
  N3: U1.D3, S1.Pin_3, S1.Pin_4, R2.Pin_1
  N4: U1.3V3, S1.Pin_1, S1.Pin_2, S2.Pin_1, S2.Pin_2
  N5: U1.GND, R2.Pin_0, R3.Pin_0
  N6: LED1.cathode, R1.Pin_1

custom parts:
  NodeMCU v3.0: NodeMCU v3 Lua WIFI Development Board
