# Fritzing sketch lm35 (saved by Fritzing 0.9.3b)
breadboards: 1

parts:
  T1 = LM35 Temperature Sensor [package="TO92 [THT]"]
  U1 = NodeMCU v3.0

nets:
  N1: T1.Vout, U1.A0

custom parts:
  NodeMCU v3.0: NodeMCU v3 Lua WIFI Development Board
