# Fritzing sketch servo (saved by Fritzing 0.9.3b)
breadboards: 1

parts:
  J1 = Basic Servo
  U1 = NodeMCU v3.0
  PSU1 = Adjustable Breadboard Power Supply

nets:
  GND: J1.gnd, U1.GND, PSU1.Vout-
  N1: J1.vcc, PSU1.Vout+
  N2: J1.pulse, U1.D1

custom parts:
  NodeMCU v3.0: NodeMCU v3 Lua WIFI Development Board
