# Fritzing sketch led_pwm (saved by Fritzing 0.9.3b)
breadboards: 1

parts:
  U1 = NodeMCU v3.0
  LED1 = LED - 5mm [color="Red (633nm)" package="5 mm [THT]"]
  R1 = Resistor [tolerance=±5% resistance=330 package=THT]
  R2 = Rotary Potentiometer (Small) [maximum_resistance=100kΩ package=THT]

nets:
  N1: U1.D1, LED1.anode
  N2: U1.3V3, R2.leg2
  N3: U1.GND, R2.leg1
  N4: U1.A0, R2.wiper
  N5: LED1.cathode, R1.Pin_1

custom parts:
  NodeMCU v3.0: NodeMCU v3 Lua WIFI Development Board
